# Fritzing sketch Bridge (saved by Fritzing 0.9.3b)

parts:
  U1 = ESP8266 WiFi Module [part_number=ESP8266]
  U2 = RXB6 Superhetrodyne receiver [part_number=RXB6 package=sip]
  U3 = AMS1117 step down module
  Onderdeel1 = Adafruit Micro USB Breakout [part_number="Adafruit #1833"]
  R1 = Resistor [tolerance=±5% resistance=220 package="0402 [SMD]"]  # not connected
  R2 = Resistor [tolerance=±5% resistance=220 package="0402 [SMD]"]  # not connected

nets:
  N1: U1.RXD, U2.DATA
  N2: U1.VCC, U2.DVCC, U3.VOUT+
  GND: U1.GND, U2.DGND, U3.GND-, Onderdeel1.GND
  N3: U3.VIN+, Onderdeel1.VBUS

custom parts:
  ESP8266 WiFi Module: Generic WiFi Module based on the ESP8266 with onboard PCB antenna and UART communications
  RXB6 Superhetrodyne receiver: RF Link receivers RXB6, 315, 433.92 Mhz (or custom) Converted from the Spartfun Rf-LINK_RX part (which doesn't apper to be quite correct).
  Adafruit Micro USB Breakout: Simple but effective - this breakout board has a USB Micro-B connector, with all 5 pins broken out. Great for pairing with a microcontroller with USB support, or adding USB 5V power to a project. We use a micro-AB connector with through-hole shielding pads for an excellent strong connection - it won't rip off by accident! Comes with one fully assembled and tested micro B breakout PCB and a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
