# Fritzing sketch Receiver (saved by Fritzing 0.9.3b)

parts:
  WeMos_D1_Mini1 = WeMos D1 Mini
  U1 = RXB6 Superhetrodyne receiver [part_number=RXB6 package=sip]

nets:
  N1: WeMos_D1_Mini1.3V3, U1.DVCC
  N2: WeMos_D1_Mini1.D2, U1.DATA
  N3: WeMos_D1_Mini1.G, U1.DGND

custom parts:
  RXB6 Superhetrodyne receiver: RF Link receivers RXB6, 315, 433.92 Mhz (or custom) Converted from the Spartfun Rf-LINK_RX part (which doesn't apper to be quite correct).
