# Fritzing sketch Uno-Flash (saved by Fritzing 0.9.3b)
breadboards: 1

parts:
  Onderdeel1 = Arduino Uno (Rev3) - ICSP
  U1 = attiny85 [package=dip]
  C1 = Electrolytic Capacitor [capacitance=10µF package="1010 [SMD, electrolytic]"]

nets:
  N1: Onderdeel1.ICSP_MISO, Onderdeel1.D12/MISO, U1.Pin_6
  N2: Onderdeel1.D10_PWM/SS, U1.Pin_1
  N3: Onderdeel1.D11_PWM/MOSI, U1.Pin_5
  N4: Onderdeel1.D13/SCK, U1.Pin_7
  N5: Onderdeel1.RESET, C1.+
  N6: Onderdeel1.5V, U1.Pin_8
  N7: Onderdeel1.GND, U1.Pin_4, C1.-
